# Fritzing sketch IDE2017 Receiver (saved by Fritzing 0.9.3b)

parts:
  Part1 = Arduino Uno (Rev3)
  Q1 = NPN-Transistor [package="TO92 [THT]"]
  J1 = Piezo Speaker
  LED1 = LED - 5mm [color="Red (633nm)" package="5 mm [THT]"]
  S1 = Pushbutton [package="[THT]"]
  S2 = Pushbutton [package="[THT]"]
  Part2 = NRF24L01+ Breakout Board
  OMRON1 = OMRON PCB Power Relay – G5LE [part_number="G5LE-1\n" package=THT]

nets:
  N1: Part1.D8, Part2.MISO
  N2: Part1.D11_PWM/MOSI, Part2.IRQ
  N3: Part1.D12/MISO, Part2.MOSI
  N4: Part1.D13/SCK, Part2.CS
  GND: Part1.GND, J1.pin1, LED1.cathode, S1.Pin_1, S1.Pin_2, S2.Pin_4, Part2.GND, OMRON1.COIL1
  N5: Part1.D2, Q1.B, LED1.anode
  N6: Part1.D3_PWM, J1.pin2
  N7: Part1.D4, S2.Pin_2
  N8: Part1.D7, Part2.SCK
  N9: Part1.RESET, S1.Pin_4
  N10: Part1.5V, Q1.E, Part2.CE
  N11: Q1.C, OMRON1.COIL2
