# Fritzing sketch IDE2017 Transmitter (saved by Fritzing 0.9.3b)

parts:
  Part1 = NRF24L01+ Breakout Board
  R1 = Resistor [tolerance=±5% resistance=220 package=THT]
  S1 = Taiway 100-SP-X-T1 SPDT Miniature Toggle Switch [part_number=100-SP-X-T1-0-0-B1-M1 package=THT]
  C1 = Ceramic Capacitor [capacitance=100nF package="100 mil [THT, multilayer]"]
  Part3 = Arduino Pro Mini v13

nets:
  GND: Part1.GND, S1.L2, C1.1, Part3.GND
  N1: Part1.CE, Part3.VCC
  N2: Part1.CS, Part3.D11_PWM/MOSI
  N3: Part1.SCK, Part3.D7
  N4: Part1.MOSI, Part3.D12/MISO
  N5: Part1.MISO, Part3.D8
  N6: Part1.IRQ, Part3.D13/SCK
  N7: R1.Pin_0, S1.L1
  N8: R1.Pin_1, C1.0, Part3.D2
